# Fritzing sketch mobile-main - backup (saved by Fritzing 0.9.3b)
circuit board: 10.7745cm x 5.51083cm
circuit board: 10.6419cm x 13.5274cm
breadboards: 1

parts:
  Arduino_Mega2560 = Arduino Mega 2560 (Rev3)
  Reset_Button = Pushbutton [package="[THT]"]
  IR_Sensor_Header = female pin header, 8 pins [form="♀ (female)"]
  HC-12 = HC-12 Connector [form="♀ (female)" package=THT]
  J1 = female pin header, 18 pins [form="♀ (female)"]
  J2 = female pin header, 18 pins [form="♀ (female)"]
  J3 = female pin header, 4 pins [form="♀ (female)"]
  TCS34725 = Generic female header - 7 pins [form="♀ (female)" package=THT]
  J4 = female pin header, 2 pins [form="♀ (female)"]
  J5 = female pin header, 2 pins [form="♀ (female)"]
  L293D = L293D [package=THT]
  J6 = Camdenboss CTB0158-2 [part_number=CTB0158-2 package=THT]
  J7 = Camdenboss CTB0158-2 [part_number=CTB0158-2 package=THT]
  J8 = female pin header, 1 pin [form="♀ (female)"]
  S1 = Pushbutton [package="[THT]"]
  S2 = Pushbutton [package="[THT]"]
  S3 = Pushbutton [package="[THT]"]
  S4 = Pushbutton [package="[THT]"]
  J9 = female pin header, 2 pins [form="♀ (female)"]
  J10 = female pin header, 2 pins [form="♀ (female)"]
  SG1 = Buzzer 12mm [package=buzzer-ccv]
  IC1 = DIP - 14 pins [chip_label=IC package="DIP (Dual Inline) [THT]"]
  IC2 = DIP - 14 pins [chip_label=IC package="DIP (Dual Inline) [THT]"]
  R1 = Trimmer Potentiometer [maximum_resistance=10kΩ package=THT]
  R2 = Trimmer Potentiometer [maximum_resistance=10kΩ package=THT]
  R3 = Trimmer Potentiometer [maximum_resistance=10kΩ package=THT]
  R4 = Trimmer Potentiometer [maximum_resistance=10kΩ package=THT]
  R5 = Trimmer Potentiometer [maximum_resistance=10kΩ package=THT]
  R6 = Trimmer Potentiometer [maximum_resistance=10kΩ package=THT]
  LED1 = LED - 3mm [color="Red (633nm)" package="3 mm [THT]"]
  LED2 = LED - 3mm [color="Red (633nm)" package="3 mm [THT]"]
  LED3 = LED - 3mm [color="Red (633nm)" package="3 mm [THT]"]
  LED4 = LED - 3mm [color="Red (633nm)" package="3 mm [THT]"]
  LED5 = LED - 3mm [color="Red (633nm)" package="3 mm [THT]"]
  LED6 = LED - 3mm [color="Red (633nm)" package="3 mm [THT]"]
  R7 = Resistor [tolerance=±5% resistance=470 package=THT]
  R8 = Resistor [tolerance=±5% resistance=470 package=THT]
  R9 = Resistor [tolerance=±5% resistance=470 package=THT]
  R10 = Resistor [tolerance=±5% resistance=470 package=THT]
  R11 = Resistor [tolerance=±5% resistance=470 package=THT]
  R12 = Resistor [tolerance=±5% resistance=470 package=THT]

nets:
  N1: Arduino_Mega2560.A8, SG1.2
  N2: Arduino_Mega2560.A0, IR_Sensor_Header.pin8
  N3: Arduino_Mega2560.A1, IR_Sensor_Header.pin7
  N4: Arduino_Mega2560.A2, IR_Sensor_Header.pin6
  N5: Arduino_Mega2560.A3, IR_Sensor_Header.pin5
  N6: Arduino_Mega2560.A4, IR_Sensor_Header.pin4
  N7: Arduino_Mega2560.A5, IR_Sensor_Header.pin3
  N8: Arduino_Mega2560.A6, IR_Sensor_Header.pin2
  N9: Arduino_Mega2560.A7, IR_Sensor_Header.pin1
  N10: Arduino_Mega2560.D21/SCL, Arduino_Mega2560.SCL, TCS34725.SCL, J4.pin1, J5.pin1
  N11: Arduino_Mega2560.D20/SDA, Arduino_Mega2560.SDA, TCS34725.SDA, J4.pin2, J5.pin2
  N12: Arduino_Mega2560.D15/RX3, HC-12.Rx#3
  N13: Arduino_Mega2560.D14/TX3, HC-12.Rx#2
  GND: Arduino_Mega2560.GND, Reset_Button.Pin_3, Reset_Button.Pin_4, HC-12.GND, J1.pin18, J2.pin18, J3.pin3, TCS34725.GND, L293D.0V, S1.Pin_1, S1.Pin_2, S2.Pin_3, S2.Pin_4, S3.Pin_3, S3.Pin_4, S4.Pin_1, S4.Pin_2, J9.pin2
  N14: Arduino_Mega2560.D12_PWM, L293D.In_2
  N15: Arduino_Mega2560.D11_PWM, L293D.In_1
  N16: Arduino_Mega2560.D10_PWM, L293D.In_4
  N17: Arduino_Mega2560.D9_PWM, L293D.Enable_2
  N18: Arduino_Mega2560.D8_PWM, L293D.In_3
  N19: Arduino_Mega2560.RESET, Reset_Button.Pin_1, Reset_Button.Pin_2
  5V: Arduino_Mega2560.5V, HC-12.Vcc, J1.pin1, J2.pin1, J3.pin4, TCS34725.Vin, L293D.+V
  N20: Arduino_Mega2560.D0_RX0, J10.pin1
  N21: Arduino_Mega2560.D1_TX0, J10.pin2
  N22: Arduino_Mega2560.D6_PWM, S2.Pin_1, S2.Pin_2
  N23: Arduino_Mega2560.D7_PWM, L293D.Enable_1
  N24: Arduino_Mega2560.D22, J2.pin2
  N25: Arduino_Mega2560.D23, J1.pin2
  N26: Arduino_Mega2560.D24, J2.pin3
  N27: Arduino_Mega2560.D25, J1.pin3
  N28: Arduino_Mega2560.D26, J2.pin4
  N29: Arduino_Mega2560.D27, J1.pin4
  N30: Arduino_Mega2560.D28, J2.pin5
  N31: Arduino_Mega2560.D29, J1.pin5
  N32: Arduino_Mega2560.D30, J2.pin6
  N33: Arduino_Mega2560.D31, J1.pin6
  N34: Arduino_Mega2560.D32, J2.pin7
  N35: Arduino_Mega2560.D33, J1.pin7
  N36: Arduino_Mega2560.D34, J2.pin8
  N37: Arduino_Mega2560.D35, J1.pin8
  N38: Arduino_Mega2560.D36, J2.pin9
  N39: Arduino_Mega2560.D37, J1.pin9
  N40: Arduino_Mega2560.D38, J2.pin10
  N41: Arduino_Mega2560.D39, J1.pin10
  N42: Arduino_Mega2560.D40, J2.pin11
  N43: Arduino_Mega2560.D41, J1.pin11
  N44: Arduino_Mega2560.D42, J2.pin12
  N45: Arduino_Mega2560.D43, J1.pin12
  N46: Arduino_Mega2560.D44, J2.pin13
  N47: Arduino_Mega2560.D45, J1.pin13
  N48: Arduino_Mega2560.D46, J2.pin14
  N49: Arduino_Mega2560.D47, J1.pin14
  N50: Arduino_Mega2560.D48, J2.pin15
  N51: Arduino_Mega2560.D49, J1.pin15
  N52: Arduino_Mega2560.D50, J2.pin16
  N53: Arduino_Mega2560.D51, J1.pin16
  N54: Arduino_Mega2560.D52, J2.pin17
  N55: Arduino_Mega2560.D53, J1.pin17
  N56: HC-12.Set, J9.pin1
  N57: L293D.Out_1_(_Controlled_by_Enable_1_), J6.pin1
  N58: L293D.Out_2_(_Controlled_by_Enable_1_), J6.pin2
  N59: L293D.+Vmotor, J8.pin1
  N60: L293D.Out_3_(_Controlled_by_Enable_2_), J7.pin1
  N61: L293D.Out_4_(_Controlled_by_Enable_2_), J7.pin2
  N62: S1.Pin_3, S1.Pin_4
  N63: S3.Pin_1, S3.Pin_2
  N64: S4.Pin_3, S4.Pin_4
  N65: IC1.OUT1, LED2.anode
  N66: IC1.IN1+, R2.wiper
  N67: IC1.V+, IC2.V+, R5.leg2, R6.leg2
  N68: IC1.IN2+, R1.wiper
  N69: IC1.OUT2, LED1.anode, R9.Pin_1
  GND_2: IC1.GND, IC2.GND, R5.leg1, R6.leg1, LED1.cathode, LED6.cathode, R7.Pin_1, R8.Pin_1, R9.Pin_0, R10.Pin_0, R11.Pin_0, R12.Pin_0
  N70: IC1.IN4+, R5.wiper
  N71: IC1.OUT4, LED3.anode
  N72: IC2.OUT1, LED4.anode
  N73: IC2.IN1+, R6.wiper
  N74: IC2.OUT3, LED6.anode, R10.Pin_1
  N75: IC2.IN3+, R4.wiper
  N76: IC2.IN4+, R3.wiper
  N77: IC2.OUT4, LED5.anode
  N78: R1.leg1, R2.leg1
  N79: R1.leg2, R2.leg2
  N80: R3.leg1, R4.leg1
  N81: R3.leg2, R4.leg2
  N82: LED2.cathode, R7.Pin_0
  N83: LED3.cathode, R8.Pin_0
  N84: LED4.cathode, R12.Pin_1
  N85: LED5.cathode, R11.Pin_1

custom parts:
  HC-12 Connector: Generic female header
  Generic female header - 7 pins: Generic female header
  DIP - 14 pins: A DIP stand-in part for whatever IC you want. With 14 pins on a 300mil dual inline package (DIP) footprint.
