# Fritzing sketch sensor-panel (saved by Fritzing 0.9.3b)
circuit board: 10cm x 2.5cm
breadboards: 1

parts:
  J1 = IR Sensor [form="♀ (female)" package=THT]
  J2 = IR Sensor [form="♀ (female)" package=THT]
  J3 = IR Sensor [form="♀ (female)" package=THT]
  J4 = IR Sensor [form="♀ (female)" package=THT]
  J5 = IR Sensor [form="♀ (female)" package=THT]
  J6 = IR Sensor [form="♀ (female)" package=THT]
  R1 = Resistor [tolerance=±5% resistance=470 package=THT]
  R2 = Resistor [tolerance=±5% resistance=470 package=THT]
  R3 = Resistor [tolerance=±5% resistance=470 package=THT]
  R5 = Resistor [tolerance=±5% resistance=1k package=THT]
  R6 = Resistor [tolerance=±5% resistance=1k package=THT]
  R7 = Resistor [tolerance=±5% resistance=1k package=THT]
  R8 = Resistor [tolerance=±5% resistance=1k package=THT]
  R9 = Resistor [tolerance=±5% resistance=1k package=THT]
  R10 = Resistor [tolerance=±5% resistance=1k package=THT]
  R11 = Resistor [tolerance=±5% resistance=470 package=THT]
  R12 = Resistor [tolerance=±5% resistance=470 package=THT]
  R13 = Resistor [tolerance=±5% resistance=470 package=THT]
  J7 = female pin header, 6 pins [form="♀ (female)"]
  J8 = female pin header, 2 pins [form="♀ (female)"]

nets:
  N1: J1.LED_-, J1.IR_-, J2.LED_-, J2.IR_-, J3.LED_-, J3.IR_-, J4.LED_-, J4.IR_-, J5.LED_-, J5.IR_-, J6.LED_-, J6.IR_-, J8.pin1
  N2: J1.LED_+, R1.Pin_1
  N3: J1.IR_+, R5.Pin_0, J7.pin1
  N4: J2.LED_+, R2.Pin_1
  N5: J2.IR_+, R6.Pin_0, J7.pin2
  N6: J3.LED_+, R3.Pin_1
  N7: J3.IR_+, R7.Pin_0, J7.pin3
  N8: J4.LED_+, R11.Pin_1
  N9: J4.IR_+, R8.Pin_0, J7.pin4
  N10: J5.LED_+, R12.Pin_1
  N11: J5.IR_+, R9.Pin_0, J7.pin5
  N12: J6.LED_+, R13.Pin_1
  N13: J6.IR_+, R10.Pin_0, J7.pin6
  N14: R1.Pin_0, R2.Pin_0, R3.Pin_0, R5.Pin_1, R6.Pin_1, R7.Pin_1, R8.Pin_1, R9.Pin_1, R10.Pin_1, R11.Pin_0, R12.Pin_0, R13.Pin_0, J8.pin2

custom parts:
  IR Sensor: IR Sensor header
